# Fritzing sketch Fritz sketch (saved by Fritzing 1.0.6)
breadboards: 1

parts:
  Part1 = Adafruit Feather RP2040 [part_number="Adafruit #4884"]
  Part2 = Adafruit Feather M0 Basic Proto [part_number="Adafruit #2772"]
  Part3 = Adafruit FeatherWing Doubler [part_number="Adafruit #2890"]
  Part4 = Adafruit NeoPXL8 FeatherWing [part_number="Adafruit #3249"]
  Part5 = Adafruit DC+Stepper FeatherWing [part_number="Adafruit #2927"]

nets:
  GND: Part1.GND, Part1.D4, Part2.GND, Part3.G, Part3.GND, Part4.GND, Part4.G, Part5.GND, Part5.G
  +3V3: Part1.+3V3, Part2.AREF, Part2.+3V3, Part3.AREF, Part3.3V, Part4.3.3V, Part4.AREF, Part5.AREF, Part5.+3.3V
  N1: Part1.SDA, Part2.SDA, Part3.SDA, Part4.SDA, Part5.SDA
  N2: Part1.SCL, Part2.SCL, Part3.SCL, Part4.SCL, Part5.SCL
  N3: Part1.TX, Part2.D1, Part3.TX, Part4.TX, Part5.TX
  N4: Part1.RX, Part2.D0, Part3.RX, Part4.RX, Part5.RX
  N5: Part1.MISO, Part2.MISO, Part3.MISO, Part4.MISO, Part5.MISO
  N6: Part1.MOSI, Part2.MOSI, Part3.MOSI, Part4.MOSI, Part5.MOSI
  N7: Part1.SCK, Part2.SCK, Part3.SCK, Part4.SCK, Part5.SCK
  N8: Part1.D25, Part2.A5, Part3.F, Part4.A5, Part5.F
  N9: Part1.D24, Part2.A4, Part3.E, Part4.A4, Part5.E
  N10: Part1.A3, Part2.A3, Part3.D, Part4.A3, Part5.D
  N11: Part1.A2, Part2.A2, Part3.C, Part4.A2, Part5.C
  N12: Part1.A1, Part2.A1, Part3.B, Part4.A1, Part5.B
  N13: Part1.A0, Part2.A0, Part3.A, Part4.A0, Part5.A
  N14: Part1.!RESET, Part2.!RESET, Part3.RESET, Part4.RESET, Part5.RESET
  N15: Part1.VBAT, Part2.VBAT, Part3.VBAT, Part4.VBAT, Part5.VBAT
  N16: Part1.EN, Part2.EN, Part3.EN, Part4.EN, Part5.EN
  N17: Part1.VUSB, Part2.VBUS, Part3.USB, Part4.USB, Part5.USB
  N18: Part1.D13, Part2.D13, Part3.O, Part4.D13, Part5.N
  N19: Part1.D12, Part2.D12, Part3.N, Part4.D12, Part5.M
  N20: Part1.D11, Part2.D11, Part3.M, Part4.D11, Part5.L
  N21: Part1.D10, Part2.D10, Part3.L, Part4.D10, Part5.K
  N22: Part1.D9, Part2.D9, Part3.K, Part4.D9, Part5.J
  N23: Part1.D6, Part2.D6, Part3.J, Part4.D6, Part5.I
  N24: Part1.D5, Part2.D5, Part3.I, Part4.D5, Part5.H

custom parts:
  Adafruit Feather RP2040: A new chip means a new Feather, and the Raspberry Pi RP2040 is no exception. When we saw this chip we thought "this chip is going to be awesome when we give it the Feather Treatment" and so we did! This Feather features the RP2040, and all niceties you know and love about Feather Measures 2.0" x 0.9" x 0.28" (50.8mm x 22.8mm x 7mm) without headers soldered in Light as a (large?) feather - 5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
  Adafruit Feather M0 Basic Proto: At the Feather M0's heart is an ATSAMD21G18 ARM Cortex M0 processor, clocked at 48 MHz and at 3.3V logic, the same one used in the new Arduino Zero. This chip has a whopping 256K of FLASH (8x more than the Atmega328 or 32u4) and 32K of RAM (16x as much)! This chip comes with built in USB so it has USB-to-Serial program & debug capability built in with no need for an FTDI-like chip. To make it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
  Adafruit FeatherWing Doubler: This is the FeatherWing Doubler - a prototyping add-on and more for all Feather boards. This is similar to our FeatherWing Proto except there are two! The magic of the Doubler comes when stacking a Feather and another board on top of the Doubler so you can work with both boards simultaneously side-by-side! The Doubler, like the Proto, has a duplicate breakout for each pin on a Feather, as well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
  Adafruit NeoPXL8 FeatherWing: Since we first started carrying NeoPixels back in 2012, the chainable RGB LEDs have taken over the world. And a big part of that success is due to the simplicity of their wiring - just one data wire, no matter how many pixels you've got. So no surprise they're everywhere, blinking away in art exhibits, maker faire demos, DJ booths, decorations and costumes. But, at some point, every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
  Adafruit DC+Stepper FeatherWing: This is the DC Motor + Stepper FeatherWing which will let you use 2 x bi-polar stepper motors or 4 x brushed DC motorx (or 1 stepper and 2 DC motors). Using our Feather Stacking Headers or Feather Female Headers you can connect a FeatherWing on top or bottom of your Feather board and let the board take flight! The original Adafruit Motorshield Kit is one of our most beloved kits, which is why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
